# Fritzing sketch skematik (saved by Fritzing 0.9.3b)
breadboards: 1

parts:
  Part1 = Arduino Nano (Rev3.0)
  LED3 = smd LED [color="Red (633nm)" package="1206 [SMD]"]
  R3 = Resistor [tolerance=±5% resistance=330 package=THT]
  R5 = Rotary Potentiometer (Large) [maximum_resistance=100kΩ package=THT]

nets:
  N1: Part1.GND, LED3.cathode, R5.leg2
  N2: Part1.5V, R5.leg1
  N3: Part1.A0, R5.wiper
  N4: Part1.D13/SCK, R3.Pin_0
  N5: LED3.anode, R3.Pin_1
